# Fritzing sketch Windmesser (saved by Fritzing 0.9.3b)
circuit board: 2.1cm x 4cm
breadboards: 1

parts:
  C1 = Ceramic Capacitor [capacitance=10µF package="100 mil [THT, multilayer]"]
  Wind = Screw terminal - 2 pins [package=THT]
  VCC = Battery
  R1 = Resistor [tolerance=±5% resistance=10k package=THT]
  Arduino = Arduino Pro Mini (3.3V)
  Funk = NRF24L01+ Breakout Board

nets:
  VCC: C1.0, Wind.pin2, VCC.+, R1.Pin_0, Arduino.VCC, Funk.VCC
  GND: C1.1, VCC.-, R1.Pin_1, Arduino.GND, Funk.GND
  N1: Wind.pin1, Arduino.D3
  N2: Arduino.SCK, Funk.SCK
  N3: Arduino.MISO, Funk.MISO
  N4: Arduino.MOSI, Funk.MOSI
  N5: Arduino.D7, Funk.CS
  N6: Arduino.D6, Funk.CE
